# Fritzing sketch ELProject1 (saved by Fritzing 1.0.4)
breadboards: 2

parts:
  M1 = DOIT Esp32 DevKit v1 (30 pins long, 11 pins width) [part_number=ESP32S-PIN30]
  R1 = Photocell (LDR) [power=0.25W dark_resistance_@0.01lx=300kΩ light_resistance_@100lx=400Ω luminance=10lx package=THT]
  R2 = Photocell (LDR) [power=0.25W dark_resistance_@0.01lx=300kΩ light_resistance_@100lx=400Ω luminance=10lx package=THT]
  R3 = Photocell (LDR) [power=0.25W dark_resistance_@0.01lx=300kΩ light_resistance_@100lx=400Ω luminance=10lx package=THT]
  R4 = Photocell (LDR) [power=0.25W dark_resistance_@0.01lx=300kΩ light_resistance_@100lx=400Ω luminance=10lx package=THT]
  R5 = Photocell (LDR) [power=0.25W dark_resistance_@0.01lx=300kΩ light_resistance_@100lx=400Ω luminance=10lx package=THT]
  R6 = Photocell (LDR) [power=0.25W dark_resistance_@0.01lx=300kΩ light_resistance_@100lx=400Ω luminance=10lx package=THT]
  R7 = Photocell (LDR) [power=0.25W dark_resistance_@0.01lx=300kΩ light_resistance_@100lx=400Ω luminance=10lx package=THT]
  R8 = Photocell (LDR) [power=0.25W dark_resistance_@0.01lx=300kΩ light_resistance_@100lx=400Ω luminance=10lx package=THT]
  R9 = Photocell (LDR) [power=0.25W dark_resistance_@0.01lx=300kΩ light_resistance_@100lx=400Ω luminance=10lx package=THT]
  R10 = Photocell (LDR) [power=0.25W dark_resistance_@0.01lx=300kΩ light_resistance_@100lx=400Ω luminance=10lx package=THT]
  R11 = Photocell (LDR) [power=0.25W dark_resistance_@0.01lx=300kΩ light_resistance_@100lx=400Ω luminance=10lx package=THT]
  R12 = Photocell (LDR) [power=0.25W dark_resistance_@0.01lx=300kΩ light_resistance_@100lx=400Ω luminance=10lx package=THT]
  R13 = Photocell (LDR) [power=0.25W dark_resistance_@0.01lx=300kΩ light_resistance_@100lx=400Ω luminance=10lx package=THT]
  R14 = Photocell (LDR) [power=0.25W dark_resistance_@0.01lx=300kΩ light_resistance_@100lx=400Ω luminance=10lx package=THT]
  R15 = Photocell (LDR) [power=0.25W dark_resistance_@0.01lx=300kΩ light_resistance_@100lx=400Ω luminance=10lx package=THT]
  R16 = Photocell (LDR) [power=0.25W dark_resistance_@0.01lx=300kΩ light_resistance_@100lx=400Ω luminance=10lx package=THT]
  R21 = Resistor [tolerance=±5% power=0.25W resistance=10k package=THT]
  R25 = Resistor [tolerance=±5% power=0.25W resistance=10k package=THT]
  R26 = Resistor [tolerance=±5% power=0.25W resistance=10k package=THT]
  R28 = Resistor [tolerance=±5% power=0.25W resistance=10k package=THT]
  R30 = Resistor [tolerance=±5% power=0.25W resistance=10k package=THT]
  R32 = Resistor [tolerance=±5% power=0.25W resistance=10k package=THT]
  R33 = Resistor [tolerance=±5% power=0.25W resistance=10k package=THT]
  R34 = Resistor [tolerance=±5% power=0.25W resistance=10k package=THT]
  R35 = Resistor [tolerance=±5% power=0.25W resistance=10k package=THT]
  R36 = Resistor [tolerance=±5% power=0.25W resistance=10k package=THT]
  R37 = Resistor [tolerance=±5% power=0.25W resistance=10k package=THT]
  R38 = Resistor [tolerance=±5% power=0.25W resistance=10k package=THT]
  R39 = Resistor [tolerance=±5% power=0.25W resistance=10k package=THT]
  R40 = Resistor [tolerance=±5% power=0.25W resistance=10k package=THT]
  R41 = Resistor [tolerance=±5% power=0.25W resistance=10k package=THT]
  R42 = Resistor [tolerance=±5% power=0.25W resistance=10k package=THT]

nets:
  N1: M1.3V3, R1.pin_1, R2.pin_1, R3.pin_1, R4.pin_1, R5.pin_1, R6.pin_1, R7.pin_1, R8.pin_1, R9.pin_1, R10.pin_1, R11.pin_1, R12.pin_1, R13.pin_1, R14.pin_1, R15.pin_1, R16.pin_1
  N2: M1.GND, R21.Pin_0, R25.Pin_0, R26.Pin_0, R28.Pin_0, R30.Pin_0, R32.Pin_0, R33.Pin_0, R34.Pin_0, R35.Pin_0, R36.Pin_0, R37.Pin_0, R38.Pin_0, R39.Pin_0, R40.Pin_0, R41.Pin_0, R42.Pin_0
  N3: R1.pin_0, R39.Pin_1
  N4: R2.pin_0, R40.Pin_1
  N5: R3.pin_0, R41.Pin_1
  N6: R4.pin_0, R42.Pin_1
  N7: R5.pin_0, R36.Pin_1
  N8: R6.pin_0, R37.Pin_1
  N9: R7.pin_0, R38.Pin_1
  N10: R8.pin_0, R21.Pin_1
  N11: R9.pin_0, R34.Pin_1
  N12: R10.pin_0, R32.Pin_1
  N13: R11.pin_0, R35.Pin_1
  N14: R12.pin_0, R33.Pin_1
  N15: R13.pin_0, R25.Pin_1
  N16: R14.pin_0, R30.Pin_1
  N17: R15.pin_0, R28.Pin_1
  N18: R16.pin_0, R26.Pin_1

custom parts:
  DOIT Esp32 DevKit v1 (30 pins long, 11 pins width): The DOIT Esp32 DevKit v1 is one of the development board created by DOIT to evaluate the ESP-WROOM-32 module. It is based on the ESP32 microcontroller that boasts Wifi, Bluetooth, Ethernet and Low Power support all in a single chip. (vanepp) made breadboard work, adjusted pin numbering and labels and reduced size of schematic and cleaned up pcb. This chip is 30pins long (2 x15) and 11 pins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
